# Fritzing sketch arduino_sound (saved by Fritzing 0.9.0b)
breadboards: 1

parts:
  Parte1 = Arduino Uno (Rev3)
  U1 = POT [package=pot_mammoth]
  U2 = POT [package=pot_mammoth]
  S2 = Momentary Switch [package=ksa_sealed_tac_switch]
  LED2 = LED - 5mm [color="Red (633nm)" package="5 mm [THT]"]
  R1 = Resistor [package="2512 [SMD]"]
  J1 = Piezo Speaker
  R2 = Resistor [package="2512 [SMD]"]

nets:
  N1: Parte1.A0, U1.A
  N2: Parte1.A2, U2.A
  N3: Parte1.D8, S2.1
  N4: Parte1.D12/MISO, J1.pin2
  N5: Parte1.D3_PWM, LED2.anode
  N6: Parte1.5V, U1.E, U2.E, S2.4
  N7: Parte1.GND, U1.S, U2.S, R1.Pin_1, J1.pin1, R2.Pin_1
  N8: S2.3, R1.Pin_0
  N9: LED2.cathode, R2.Pin_0
